# Fritzing sketch 28BYJ-48-driver_and_motor (saved by Fritzing 0.9.6b)

parts:
  Driver1 = 28BYJ-48 Driver Module [part_number=ULN2003 package=THT]
  SM1 = 28BYJ-48 Stepper Motor [part_number=28BYJ-48]
  Arduino = Arduino Uno (Rev3)

nets:
  N1: Driver1.IN1, Arduino.D11_PWM/MOSI
  N2: Driver1.IN2, Arduino.D10_PWM/SS
  N3: Driver1.IN3, Arduino.D9_PWM
  N4: Driver1.IN4, Arduino.D8
  N5: Driver1.blue-pin, SM1.blue-pin
  N6: Driver1.pink-pin, SM1.pink-pin
  N7: Driver1.yellow-pin, SM1.yellow-pin
  N8: Driver1.orange-pin, SM1.orange-pin
  N9: Driver1.red-pin, SM1.red-pin

custom parts:
  28BYJ-48 Driver Module: Generic male header
  28BYJ-48 Stepper Motor: Unipolar Stepper Motor 28BYJ-48 Top coil - pink & orange Bottom coil - blue & yellow Common rail - red Connector pins: blue - pink - yellow - orange - red
