# Fritzing sketch Niels Janssen OrangePi (saved by Fritzing 0.9.3b)
breadboards: 1

parts:
  Orange_Pi_One1 = Orange Pi One [part_number=OPI-ONE]
  BREAKOUT1 = ULN2003A breakout board
  S2 = Pushbutton [package="[SMD]"]
  R1 = Resistor [tolerance=±5% resistance=220 package="0603 [SMD]"]
  R3 = Resistor [tolerance=±5% resistance=220 package="0603 [SMD]"]
  R4 = Resistor [tolerance=±5% resistance=220 package="0603 [SMD]"]
  LED1 = RGB LED (com. anode, rbg) [package="5 mm [THT]"]
  Part1 = GY-BMEP280 Barometric Pressure Sensor - Breakout
  Part2 = BH1750

nets:
  N1: Orange_Pi_One1.PA11, R1.Pin_1
  N2: Orange_Pi_One1.GND, BREAKOUT1.In_1, BREAKOUT1.In_3, S2.Pin_1, S2.Pin_2
  N3: Orange_Pi_One1.PA13, BREAKOUT1.In_2
  N4: Orange_Pi_One1.PA1, R3.Pin_1
  N5: Orange_Pi_One1.PA3, R4.Pin_1
  N6: Orange_Pi_One1.PA10, BREAKOUT1.0V, S2.Pin_3, S2.Pin_4, LED1.green_cathode, Part1.CSB, Part2.GND
  N7: Orange_Pi_One1.PG9, Part1.SDA, Part2.SCL
  N8: Orange_Pi_One1.PG6, Part1.SCL, Part2.SDA
  +5V: Orange_Pi_One1.PG7, BREAKOUT1.+5V, Part1.SDO, Part2.VCC
  N9: Orange_Pi_One1.5V, BREAKOUT1.In_4
  N10: R1.Pin_0, LED1.common_anode
  N11: R3.Pin_0, LED1.red_cathode
  N12: R4.Pin_0, LED1.blue_cathode

custom parts:
  Orange Pi One: It’s an open-source single-board computer. It can run Android 4.4, Ubuntu, Debian, Rasberry Pi Image, as well as the banana pi Image. It uses the AllWinner H3 SoC, and has 512MB DDR3 SDRAM
  ULN2003A breakout board: ULN2003A 7-way Darlington Transistor Driver on breakoutboard
  GY-BMEP280 Barometric Pressure Sensor - Breakout: The BME280 is a chip which was originally designed for the next generation of smartphones. It is made up of a very accurate pressure sensor and an associated temperature sensor which helps calibrate the pressure readings. And just for fun they threw in a pretty solid humidity sensor in there as well! So with an I2C connection you have access to enough weather data to make some pretty good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
  BH1750: Light Sensor
