# Fritzing sketch Niels Janssen Pico (saved by Fritzing 0.9.3b)
breadboards: 1

parts:
  Mod1 = Raspberry Pi Pico
  R1 = Resistor [tolerance=±5% resistance=220 package="0603 [SMD]"]
  LED1 = LED - 3mm [color="Red (633nm)" package="3 mm [THT]"]
  Nokia_5110_LCD_Module1 = Nokia 5110 LCD
  Part1 = GY-BMEP280 Barometric Pressure Sensor - Breakout

nets:
  N1: Mod1.pin_7, Nokia_5110_LCD_Module1.DN(MOSI), Nokia_5110_LCD_Module1.DN(MODI)_(out)
  N2: Mod1.pin_9, Nokia_5110_LCD_Module1.GND, Nokia_5110_LCD_Module1.GND_(out)
  N3: Mod1.pin_10, Nokia_5110_LCD_Module1.SCE, Nokia_5110_LCD_Module1.SCE_(out)
  N4: Mod1.pin_11, Nokia_5110_LCD_Module1.D/C, Nokia_5110_LCD_Module1.D/C_(out)
  N5: Mod1.pin_12, Nokia_5110_LCD_Module1.VCC, Nokia_5110_LCD_Module1.VCC_(out)
  N6: Mod1.pin_13, Mod1.pin_23, Mod1.pin_28, Mod1.pin_38, Mod1.pin_42, LED1.cathode, Part1.CSB
  N7: Mod1.pin_20, R1.Pin_1
  N8: Mod1.pin_21, Part1.SCL
  N9: Mod1.pin_22, Part1.SDA
  N10: Mod1.pin_24, Nokia_5110_LCD_Module1.SCLK
  N11: Mod1.pin_36, Nokia_5110_LCD_Module1.LED, Part1.SDO

custom parts:
  Raspberry Pi Pico: Raspberry Pi Pico. Based around the RP2040 microcontroller the Pico is a low cost microcontroller device bringing Raspberry Pi quality, cost, and easy of use to the microcontroller space. Jan 2021, Split part in to two versions: SMD (this one) and tht. This one is single sided and uses the castellation pads to solder the module to the board (no holes, other than for the USB connector!). The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
  Nokia 5110 LCD: Nokia 5110 Graphic 84*48 LCD module such as the Sparkfun LCD-10168 or the clones from Ebay. There is example code for the Arduino available from the Sparkfun site in https://learn.sparkfun.com/tutorials/graphic-lcd-hookup-guide This is a 3.3V device, if you are running it from a 5V micro you need a 5V tolorant level translator such as the 74ahc367 to protect the signal imputs. Rafa G. did a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
  GY-BMEP280 Barometric Pressure Sensor - Breakout: The BME280 is a chip which was originally designed for the next generation of smartphones. It is made up of a very accurate pressure sensor and an associated temperature sensor which helps calibrate the pressure readings. And just for fun they threw in a pretty solid humidity sensor in there as well! So with an I2C connection you have access to enough weather data to make some pretty good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
